# Fritzing sketch Sketch (saved by Fritzing 0.9.4)
breadboards: 1

parts:
  WeMos_D1_Mini1 = WeMos D1 Mini
  DHT22 = DHT22 Humidity and Temperature Sensor
  R1 = Resistor [tolerance=±5% resistance=10k package=THT]

nets:
  3V3: WeMos_D1_Mini1.3V3, DHT22.VDD, R1.Pin_1
  N1: WeMos_D1_Mini1.D2, DHT22.DATA, R1.Pin_0
  N2: WeMos_D1_Mini1.G, DHT22.GND
